# Fritzing sketch My Robot (saved by Fritzing 0.9.3b)

parts:
  S1 = H-Bridge with L298N
  Bauteil1 = Arduino Uno (Rev3)
  M1 = DC Motor
  M2 = DC Motor
  J1 = Basic Servo
  J2 = Basic Servo
  hc-sr1 = hc-sr04
  U1 = LIPO-2000mAh [package=lipo-2000]

nets:
  GND: S1.GND, Bauteil1.GND, J1.gnd, J2.gnd, hc-sr1.GND, U1.-
  5V: S1.5V, Bauteil1.VIN, U1.+
  N1: S1.ENA, Bauteil1.D10_PWM/SS
  N2: S1.IN1, Bauteil1.D5_PWM
  N3: S1.IN2, Bauteil1.D4
  N4: S1.IN3, Bauteil1.D2
  N5: S1.IN4, Bauteil1.D3_PWM
  N6: S1.ENB, Bauteil1.D9_PWM
  N7: S1.M1-01, M2.pin_2
  N8: S1.M1-02, M2.pin_1
  N9: S1.M2-01, M1.pin_1
  N10: S1.M2-02, M1.pin_2
  N11: Bauteil1.A0, hc-sr1.Trig
  N12: Bauteil1.A1, hc-sr1.Echo
  N13: Bauteil1.D12/MISO, J2.pulse
  N14: Bauteil1.D13/SCK, J1.pulse
  VCC: Bauteil1.5V, J1.vcc, J2.vcc, hc-sr1.VCC

custom parts:
  H-Bridge with L298N: h-bridge
